# Fritzing sketch Connections (saved by Fritzing 0.9.3b)
breadboards: 1

parts:
  Raspberry_Pi_1 = Raspberry Pi 3 [part_number=RPI-3-V1.2]
  Part1 = Arduino Uno (Rev3)
  Part2 = Logic Level Converter
  Steering_PWM_In = Antenna
  Throttle_PWM_In = Antenna
  Throttle = DC Motor
  Steering = DC Motor

nets:
  3V3: Raspberry_Pi_1.3v3, Raspberry_Pi_1.3V3, Part2.LV
  GND: Raspberry_Pi_1.GND, Part1.GND, Part2.GND
  N1: Raspberry_Pi_1.GPIO25, Part1.D7
  N2: Raspberry_Pi_1.GPIO24, Part1.D5_PWM
  N3: Raspberry_Pi_1.GPIO23, Part1.D4
  N4: Raspberry_Pi_1.GPIO15, Part2.RX2_LV
  N5: Raspberry_Pi_1.GPIO14, Part2.TX_LV
  N6: Part1.A4/SDA, Steering_PWM_In.antenna_lead
  N7: Part1.A5/SCL, Throttle_PWM_In.antenna_lead
  N8: Part1.D9_PWM, Steering.pin_1
  N9: Part1.D11_PWM/MOSI, Throttle.pin_1
  N10: Part1.D0/RX, Part2.RX2_HV
  N11: Part1.D1/TX, Part2.TX2_HV
  N12: Part1.5V, Part2.HV
